# Fritzing sketch schematic (saved by Fritzing 0.9.3b)
breadboards: 1

parts:
  DFRobot_DFPlayer_Mini1 = DFRobot DFPlayer Mini [part_number=DFR0299]
  SP1 = SPEAKER [package=pcb_mount_speaker]
  S1 = Round Pushbutton
  S2 = Round Pushbutton
  S3 = Round Pushbutton
  S4 = Round Pushbutton
  S5 = Round Pushbutton
  S6 = Round Pushbutton
  S7 = Round Pushbutton
  S8 = Round Pushbutton
  S9 = Round Pushbutton
  S10 = Round Pushbutton
  S11 = Round Pushbutton
  S12 = Round Pushbutton
  S13 = Round Pushbutton
  R1 = Resistor [tolerance=±5% resistance=0 package=THT]
  R2 = Resistor [tolerance=±5% resistance=3k package=THT]
  R3 = Resistor [tolerance=±5% resistance=6.2k package=THT]
  R4 = Resistor [tolerance=±5% resistance=9.1k package=THT]
  R5 = Resistor [tolerance=±5% resistance=33k package=THT]
  R6 = Resistor [tolerance=±5% resistance=0 package=THT]
  R7 = Resistor [tolerance=±5% resistance=3k package=THT]
  R8 = Resistor [tolerance=±5% resistance=6.2k package=THT]
  R9 = Resistor [tolerance=±5% resistance=9.1k package=THT]
  R10 = Resistor [tolerance=±5% resistance=15k package=THT]
  R11 = Resistor [tolerance=±5% resistance=24k package=THT]
  R12 = Resistor [tolerance=±5% resistance=33k package=THT]
  VCC1 = Battery

nets:
  N1: DFRobot_DFPlayer_Mini1.VCC, VCC1.+
  N2: DFRobot_DFPlayer_Mini1.SPK_1, SP1.-
  N3: DFRobot_DFPlayer_Mini1.GND-1, DFRobot_DFPlayer_Mini1.GND-2, S1.leg0, S2.leg1, S3.leg1, S4.leg1, S5.leg1, S6.leg1, S7.leg1, S8.leg0, S9.leg0, S10.leg0, S11.leg0, S12.leg0, S13.leg0
  N4: DFRobot_DFPlayer_Mini1.SPK_2, SP1.+
  N5: DFRobot_DFPlayer_Mini1.ADKEY_1, R5.Pin_0
  N6: DFRobot_DFPlayer_Mini1.ADKEY_2, R6.Pin_0, R7.Pin_0, R8.Pin_0, R9.Pin_0, R10.Pin_0, R11.Pin_0, R12.Pin_0
  N7: S1.leg1, VCC1.-
  N8: S2.leg0, R6.Pin_1
  N9: S3.leg0, R7.Pin_1
  N10: S4.leg0, R8.Pin_1
  N11: S5.leg0, R10.Pin_1
  N12: S6.leg0, R11.Pin_1
  N13: S7.leg0, R12.Pin_1
  N14: S8.leg1, R9.Pin_1
  N15: S9.leg1, R1.Pin_1
  N16: S10.leg1, R4.Pin_1
  N17: S11.leg1, R3.Pin_1
  N18: S12.leg1, R2.Pin_1
  N19: S13.leg1, R5.Pin_1
  N20: R1.Pin_0, R2.Pin_0, R3.Pin_0, R4.Pin_0
